# Fritzing sketch wiring - Master Node (saved by Fritzing 0.9.3b)

parts:
  Raspberry_Pi_1 = Raspberry Pi 3 [part_number=RPI-3-V1.2]
  Part3 = NRF24L01
  C2 = Electrolytic Capacitor [capacitance=122µF voltage=50V package="100 mil [THT, electrolytic]"]

nets:
  3V3: Raspberry_Pi_1.3v3, Part3.VCC, C2.+
  N1: Raspberry_Pi_1.GIPO17, Part3.CE
  N2: Raspberry_Pi_1.GIPO10, Part3.MOSI
  N3: Raspberry_Pi_1.GIPO9, Part3.MISO
  N4: Raspberry_Pi_1.GIPO11, Part3.SCK
  N5: Raspberry_Pi_1.GIPO8, Part3.CSN
  GND: Raspberry_Pi_1.GND, Part3.GND, C2.-
