# Fritzing sketch wiring - Nodes 1 & 6 (saved by Fritzing 0.9.3b)
breadboards: 1

parts:
  Part2 = NRF24L01
  Node_0_-_Master = Arduino Uno (Rev3) - ICSP
  C1 = Electrolytic Capacitor [capacitance=122µF voltage=50V package="100 mil [THT, electrolytic]"]
  Part3 = RFID-RC522-v2
  VCC3 = Battery
  VCC4 = Battery
  U2 = SWITCH_SPDT [package=kps-1290]

nets:
  N1: Part2.MOSI, Node_0_-_Master.ICSP_MOSI
  N2: Part2.CSN, Node_0_-_Master.D8
  VCC: Part2.VCC, Node_0_-_Master.3V3, C1.+
  N3: Part2.MISO, Node_0_-_Master.ICSP_MISO
  N4: Part2.SCK, Node_0_-_Master.ICSP_SCK
  N5: Part2.CE, Node_0_-_Master.D9_PWM
  GND: Part2.GND, Node_0_-_Master.GND, C1.-, Part3.GND, VCC3.-
  N6: Node_0_-_Master.D10_PWM/SS, Part3.SDA
  N7: Node_0_-_Master.D11_PWM/MOSI, Part3.MOSI
  N8: Node_0_-_Master.D12/MISO, Part3.MISO
  N9: Node_0_-_Master.D13/SCK, Part3.SCK
  N10: Node_0_-_Master.D5_PWM, Part3.RST
  N11: Node_0_-_Master.5V, Part3.3_3V
  N12: Node_0_-_Master.VIN, U2.O
  N13: VCC3.+, VCC4.-
  N14: VCC4.+, U2.P

custom parts:
  RFID-RC522-v2: A simple China made RFID-RC522 Reader; do check the pin labels, as this is a MFRC522 based clone.
