# Fritzing sketch wiring - Nodes 2-5 (saved by Fritzing 0.9.3b)
breadboards: 1

parts:
  Part2 = NRF24L01
  Node_0_-_Master = Arduino Uno (Rev3) - ICSP
  C1 = Electrolytic Capacitor [capacitance=122µF voltage=50V package="100 mil [THT, electrolytic]"]
  LD1 = LD
  hc-sr1 = hc-sr04
  RHT1 = Humidity and Temperature Sensor RHT03
  LED1 = LED - 5mm [color="Red (633nm)" package="5 mm [THT]"]
  R3 = Resistor [tolerance=±5% resistance=220 package=THT]
  R2 = Resistor [tolerance=±5% resistance=1M package=THT]
  hc-sr2 = hc-sr04
  Q1 = LTR-301 [package=ltr-301]
  VCC1 = Battery
  VCC2 = Battery
  U1 = SWITCH_SPDT [package=kps-1290]

nets:
  N1: Part2.MOSI, Node_0_-_Master.ICSP_MOSI
  N2: Part2.CSN, Node_0_-_Master.D8
  VCC: Part2.VCC, Node_0_-_Master.3V3, C1.+
  N3: Part2.MISO, Node_0_-_Master.ICSP_MISO
  N4: Part2.SCK, Node_0_-_Master.ICSP_SCK
  N5: Part2.CE, Node_0_-_Master.D9_PWM
  N6: Part2.GND, C1.-
  N7: Node_0_-_Master.A2, LD1.anode
  N8: Node_0_-_Master.A3, R2.Pin_0, Q1.E
  N9: Node_0_-_Master.D2, hc-sr1.Trig
  N10: Node_0_-_Master.D3_PWM, hc-sr1.Echo
  N11: Node_0_-_Master.D4, hc-sr2.Trig
  N12: Node_0_-_Master.D5_PWM, hc-sr2.Echo
  N13: Node_0_-_Master.D6_PWM, LED1.anode
  N14: Node_0_-_Master.D7, RHT1.Data-signal
  VCC_2: Node_0_-_Master.5V, hc-sr1.VCC, RHT1.Vcc, hc-sr2.VCC, Q1.C
  GND: Node_0_-_Master.GND, LD1.cathode, hc-sr1.GND, RHT1.GND_2, R3.Pin_1, R2.Pin_1, hc-sr2.GND, VCC1.-
  N15: Node_0_-_Master.VIN, U1.S
  N16: LED1.cathode, R3.Pin_0
  N17: VCC1.+, VCC2.-
  N18: VCC2.+, U1.P

custom parts:
  LD: A Generic Red Dot Laser Diode Module (~5mW)
